# Fritzing sketch Tripe-board-exercice (saved by Fritzing 1.0.1rc)
stripboards: 1

parts:
  LED1 = LED - 5mm [color="Red (633nm)" current=0.030A package="5 mm [THT]"]
  Composant1 = Arduino Uno (Rev3)
  R1 = Resistor [tolerance=±5% power=0.25W resistance=220 package=THT]

nets:
  N1: LED1.cathode, Composant1.GND
  N2: LED1.anode, R1.Pin_0
  N3: Composant1.D13/SCK, R1.Pin_1
