# Fritzing sketch moji-electro-scheme (saved by Fritzing 1.0.1rc)

parts:
  Composant1 = Arduino Uno (Rev3) - ICSP
  Composant2 = Thermal Printer
  Composant3 = RFID-RC522-v2
  Composant4 = RFID-RC522-v2
  Composant5 = RFID-RC522-v2
  Composant6 = RFID-RC522-v2
  BB1 = 4-Line Bi-Directional Level Shifter
  BB2 = 4-Line Bi-Directional Level Shifter
  JACK1 = 2.1mm Barrel Jack with Terminal Block
  JACK2 = 2.1mm Barrel Jack with Terminal Block
  V1 = DC Power [voltage=5]  # not connected

nets:
  N1: Composant1.D8, BB1.B1
  N2: Composant1.D11_PWM/MOSI, BB1.B2
  N3: Composant1.D12/MISO, BB1.B3
  N4: Composant1.D13/SCK, BB1.B4
  N5: Composant1.GND, Composant2.GND#2, BB1.GND#16, BB2.GND#16, JACK2.NEG
  N6: Composant1.D2, BB2.B1
  N7: Composant1.D3_PWM, BB2.B2
  N8: Composant1.D4, BB2.B3
  N9: Composant1.D5_PWM, BB2.B4
  N10: Composant1.5V, BB1.HV, BB2.HV
  N11: Composant2.VH, JACK2.POS
  N12: Composant3.SDA, BB2.A1
  N13: Composant3.SCK, Composant4.SCK, Composant5.SCK, Composant6.SCK, BB1.A4
  N14: Composant3.MOSI, Composant4.MOSI, Composant5.MOSI, Composant6.MOSI, BB1.A2
  N15: Composant3.MISO, Composant4.MISO, Composant5.MISO, Composant6.MISO, BB1.A3
  GND: Composant3.GND, Composant4.GND, Composant5.GND, Composant6.GND, BB1.GND#6, BB2.GND#6, JACK1.NEG
  N16: Composant3.RST, Composant4.RST, Composant5.RST, Composant6.RST, BB1.A1
  3.3V: Composant3.3.3V, Composant4.3.3V, Composant5.3.3V, Composant6.3.3V, BB1.LV, BB2.LV, JACK1.POS
  N17: Composant4.SDA, BB2.A2
  N18: Composant5.SDA, BB2.A3
  N19: Composant6.SDA, BB2.A4

custom parts:
  RFID-RC522-v2: A simple China made RFID-RC522 Reader; do check the pin labels, as this is a MFRC522 based clone.
  4-Line Bi-Directional Level Shifter: 4-Channel Bi-Directional Level Shifter
